# Fritzing sketch SpinBike (saved by Fritzing 0.8.7b)

parts:
  Raspberry_Pi_1 = Raspberry Pi 3 [part_number=RPI-3-V1.2]
  S1 = H-Bridge with L298N
  Part1 = KY-003 Hall Magnetic Sensor Module [package="Breakout board"]
  Part2 = HX711 Weighing Sensor Module
  M1 = Stepper Motor - Bipolar
  S2 = Round Pushbutton
  S3 = Round Pushbutton
  R2 = Resistor [tolerance=±5% resistance=10k package=THT]

nets:
  3V3: Raspberry_Pi_1.3v3, Raspberry_Pi_1.3V3, Part1.Vin, R2.Pin_0
  GND: Raspberry_Pi_1.GND, S1.GND, Part1.-, Part2.GND
  N1: Raspberry_Pi_1.GIPO17, S1.IN2
  N2: Raspberry_Pi_1.GIPO27, S1.IN3
  N3: Raspberry_Pi_1.GIPO5, Part2.DO/RX
  N4: Raspberry_Pi_1.GIPO6, Part2.CK/TX
  N5: Raspberry_Pi_1.GIPO13, S2.leg1
  N6: Raspberry_Pi_1.GIPO26, Part1.S
  N7: Raspberry_Pi_1.GIPO16, S3.leg1
  N8: Raspberry_Pi_1.GIPO23, S1.IN4
  N9: Raspberry_Pi_1.GIPO18, S1.IN1
  5V: Raspberry_Pi_1.5V, Part2.VCC
  N10: S1.OUT4-Motor2, M1.B
  N11: S1.OUT1-Motor1, M1.A
  N12: S1.OUT2-Motor1, M1.C
  N13: S2.leg0, S3.leg0, R2.Pin_1

notes:
  12 v DC
  Hall Sensor
  Load cell controller
  Stepper motor controller
  Raspberry PI 3 B+
  Stepper Motor
  Load Cell
  Gear shift buttons
  Power supply
  10k

custom parts:
  H-Bridge with L298N: h-bridge
  KY-003 Hall Magnetic Sensor Module: KEYES KY-003 Arduino Hall Magnetic Sensor Module is a switch that will turn on/off in the presence of a magnetic field.
